// Digital circuit cl_latch_enable.dig as structural Verilog
module cl_latch_enable (
  input  nstrb,
  input  nq_in,
  input  q_in,
  input  lr,
  output le
);

  wire multiplexer_1_out, not_1_out;

  not not_1 (not_1_out, nstrb);
  Multiplexer multiplexer_1 (.sel(lr), .in_0(q_in), .in_1(nq_in), .out(multiplexer_1_out));
  and and_1 (le, not_1_out, multiplexer_1_out);

  // Notes on the sheet:
  //   le: Latch Enable signal., pin 23
  //   nstrb: pin 11
  //   nq_in: The inverse input.
  //   q_in: The input.
  //   lr: Left or right channel?, pin 10
endmodule
