// Digital circuit clock2strobe.dig as structural Verilog
module clock2strobe (
  input  clk,
  output nSTROBE
);

  wire t_ff_1_q;

  T_FF t_ff_1 (.T(clk), .C(clk), .Q(t_ff_1_q));  // open: nQ
  or or_1 (nSTROBE, clk, t_ff_1_q);
endmodule
