// Digital circuit complete_latch.dig as structural Verilog
module complete_latch (
  input  busy_in,
  input  nstrb,
  input  d_0,
  input  d_1,
  input  d_2,
  input  d_3,
  input  d_4,
  input  d_5,
  input  d_6,
  input  d_7,
  input  lr,
  output q_0,
  output q_1,
  output q_2,
  output q_3,
  output q_4,
  output q_5,
  output q_6,
  output q_7,
  output busy_out
);

  wire LE, sl_nq, sl_q;

  JK_FF sl (.J(1'b1), .C(nstrb), .K(1'b1), .Q(sl_q), .nQ(sl_nq));
  Register #(.Bits(8)) q (
    .D({d_7, d_6, d_5, d_4, d_3, d_2, d_1, d_0}), .C(nstrb), .en(LE),
    .Q({q_7, q_6, q_5, q_4, q_3, q_2, q_1, q_0}));
  cl_latch_enable cl_le (.nstrb(nstrb), .nq_in(sl_q), .q_in(sl_nq), .lr(lr), .le(LE));
  or or_1 (busy_out, LE, busy_in);
  // Probe le on LE

  // Other names for the same wires on the sheet: nstrobe = nstrb

  // Notes on the sheet:
  //   busy_in: pin 11
  //   q_0: Output data, pin 22
  //   nstrb: pin 1, Hz: 2
  //   d_0: pin 2
  //   d_1: pin 3
  //   d_2: pin 4
  //   d_3: pin 5
  //   d_4: pin 6
  //   d_5: pin 7
  //   d_6: pin 8
  //   q_1: Output data, pin 21
  //   q_2: Output data, pin 20
  //   q_3: Output data, pin 19
  //   q_4: Output data, pin 18
  //   q_5: Output data, pin 17
  //   q_6: Output data, pin 16
  //   d_7: pin 9
  //   q_7: Output data, pin 15
  //   lr: Left or right channel configuration., pin 10
  //   busy_out: pin 14
endmodule
