// Digital circuit latch_signals.dig as structural Verilog
module latch_signals (
  input  clk,
  input  nINIT,
  input  [7:0] seed,
  output [7:0] Left,
  output [7:0] Right
);

  wire Busy, button_1_out, complete_latch_1_busy_out, nstrobe;
  wire [7:0] d;

  PRNG #(.Bits(8)) prng_1 (.S(seed), .se(button_1_out), .ne(Busy), .C(nstrobe), .R(d));
  Button button_1 (.out(button_1_out));
  // Probe d on d
  clock2strobe clock2strobe_1 (.clk(clk), .nSTROBE(nstrobe));
  // Probe ~STROBE on nstrobe
  complete_latch complete_latch_1 (
    .busy_in(1'b0), .nstrb(nstrobe), .d_0(d[0]), .d_1(d[1]), .d_2(d[2]), .d_3(d[3]), .d_4(d[4]), .d_5(d[5]),
    .d_6(d[6]), .d_7(d[7]), .lr(1'b1), .q_0(Left[0]), .q_1(Left[1]), .q_2(Left[2]), .q_3(Left[3]),
    .q_4(Left[4]), .q_5(Left[5]), .q_6(Left[6]), .q_7(Left[7]), .busy_out(complete_latch_1_busy_out));
  complete_latch complete_latch_2 (
    .busy_in(complete_latch_1_busy_out), .nstrb(nstrobe), .d_0(d[0]), .d_1(d[1]), .d_2(d[2]), .d_3(d[3]),
    .d_4(d[4]), .d_5(d[5]), .d_6(d[6]), .d_7(d[7]), .lr(1'b0), .q_0(Right[0]), .q_1(Right[1]),
    .q_2(Right[2]), .q_3(Right[3]), .q_4(Right[4]), .q_5(Right[5]), .q_6(Right[6]), .q_7(Right[7]),
    .busy_out(Busy));

  // Notes on the sheet:
  //   nINIT: default 1
  //   seed: default 13
endmodule
